# Fritzing sketch HardwareDiagram (saved by Fritzing 1.0.4)
circuit board: 23.4247cm x 14.0425cm
breadboards: 2

parts:
  U1 = LCD-16X2 [package=lcd-16x2_noholes]
  U2 = LCD-16X2 [package=lcd-16x2_noholes]
  TX = Arduino Uno (Rev3) - ICSP
  RX = Arduino Uno (Rev3) - ICSP
  R1 = Resistor [tolerance=±5% power=0.25W resistance=220 package=THT]
  R2 = Resistor [tolerance=±5% power=0.25W resistance=220 package=THT]
  R3 = Resistor [tolerance=±5% power=0.25W resistance=220 package=THT]
  R4 = Resistor [tolerance=±5% power=0.25W resistance=220 package=THT]
  RX_DATA_LED = LED - 3mm [color="Red (633nm)" current=0.030A package="3 mm [THT]"]
  RX_CLK_LED = LED - 3mm [color="Red (633nm)" current=0.030A package="3 mm [THT]"]
  TX_DATA_LED = LED - 3mm [color="Red (633nm)" current=0.030A package="3 mm [THT]"]
  TX_CLK_LED = LED - 3mm [color="Red (633nm)" current=0.030A package="3 mm [THT]"]

nets:
  N1: U1.VSS, TX.A5/SCL
  N2: U1.VDD, TX.A4/SDA, TX.ICSP_MISO, TX.D12/MISO
  GND: U1.VO, U2.VO, TX.GND, RX.GND, R1.Pin_1, R2.Pin_1, R3.Pin_0, R4.Pin_0
  N3: U1.RS, TX.5V
  N4: U2.VSS, RX.A5/SCL
  N5: U2.VDD, RX.A4/SDA
  N6: U2.RS, RX.5V
  N7: TX.D2, RX.D2, RX_CLK_LED.anode, TX_CLK_LED.anode
  N8: TX.D3_PWM, RX.D3_PWM, R3.Pin_1, RX_DATA_LED.cathode, RX_DATA_LED.anode, TX_DATA_LED.anode
  N9: R1.Pin_0, TX_CLK_LED.cathode
  N10: R2.Pin_0, TX_DATA_LED.cathode
  N11: R4.Pin_1, RX_CLK_LED.cathode
